# Fritzing sketch Power supply (saved by Fritzing 0.9.3b)
breadboards: 1

parts:
  U1 = Transformer [package=transformer]
  D1 = Rectifier Diode [part_number=1N4001 package="300 mil [THT]"]
  D2 = Rectifier Diode [part_number=1N4001 package="300 mil [THT]"]
  D3 = Rectifier Diode [part_number=1N4001 package="300 mil [THT]"]
  D4 = Rectifier Diode [part_number=1N4001 package="300 mil [THT]"]
  C1 = Electrolytic Capacitor [capacitance=100µF package="200 mil [THT, electrolytic]"]
  C2 = Electrolytic Capacitor [capacitance=1µF package="100 mil [THT, electrolytic]"]
  U2 = Voltage Regulator [package=to220-adj]
  R1 = Resistor [tolerance=±5% resistance=220 package="2512 [SMD]"]
  R2 = Rotary Potentiometer (Large) [maximum_resistance=10kΩ package=THT]
  C3 = Electrolytic Capacitor [capacitance=100µF package="200 mil [THT, electrolytic]"]
  R3 = Resistor [tolerance=±20% resistance=1k package="1206 [SMD]"]
  Power_plug1 = Power plug

nets (from the schematic view):
  N1: U1.1, Power_plug1.VCC
  N2: U1.2, Power_plug1.GND
  N3: U1.3, D3.cathode, D4.anode
  N4: U1.4, D1.cathode, D2.anode
  N5: D1.anode, D3.anode, C1.-, C2.-, R2.leg1, C3.-, R3.Pin_1
  N6: D2.cathode, D4.cathode, C1.+, C2.+, U2.IN
  N7: U2.ADJ, R1.Pin_1, R2.leg2
  N8: U2.OUT, R1.Pin_0, C3.+, R3.Pin_0

notes:
  Group 3 - Power Supply Design with LM317
